# Fritzing sketch Rain drop Sensor with Servo motor Schematic (saved by Fritzing 0.8.7b)
breadboards: 1

parts:
  Mod1 = YL-83 Rain Sensor - Control Board
  Mod2 = YL-83 Rain Sensor - Detection Board
  Part1 = Arduino Uno (Rev3)
  SERVO1 = Tower Pro SG90 servo [part_number=101246]

nets:
  VCC: Mod1.VCC, Part1.5V, SERVO1.+5V
  GND: Mod1.GND, Part1.GND, SERVO1.GND
  N1: Mod1.AO, Part1.D4
  N2: Mod1.NEG, Mod2.POS
  N3: Part1.D5_PWM, SERVO1.Signal

notes:
  Red Wire 5V
  Black Wire Gnd
  Yellow =Signal

custom parts:
  YL-83 Rain Sensor - Control Board: The YL-83 is a rain sensor that has more resistance when dry and less resistance when wet. The module runs at 5V.
  YL-83 Rain Sensor - Detection Board: The YL-83 is a rain sensor that has more resistance when dry and less resistance when wet. The module runs at 5V.
  Tower Pro SG90 servo: Original file by John De Cristofaro http://www.adafruit.com/products/1449 Adafruit Feedback Servo (Small) Edited by: e-radionica.com 28/9/2015
